# Fritzing sketch circuit (saved by Fritzing 0.9.6b)
breadboards: 1

parts:
  U1 = ESP8266 NodeMCU LoLin module
  LED1 = smd LED [color="Red (633nm)" package="0603 [SMD]"]
  J1 = Piezo Speaker
  LED2 = LEDs [package=led10mm]
  R1 = Resistor [tolerance=±5% resistance=220 package="2512 [SMD]"]
  R2 = Resistor [tolerance=±5% resistance=220 package="2512 [SMD]"]
  R3 = Resistor [tolerance=±5% resistance=220 package="2512 [SMD]"]

nets:
  N1: U1.D0, LED1.anode
  N2: U1.D1, LED2.A
  N3: U1.D3, J1.pin2
  N4: U1.GND, R1.Pin_1, R2.Pin_1, R3.Pin_1
  N5: LED1.cathode, R2.Pin_0
  N6: J1.pin1, R3.Pin_0
  N7: LED2.C, R1.Pin_0

custom parts:
  ESP8266 NodeMCU LoLin module: ESP8266 based NodeMCU
